# Fritzing sketch rc-car-lights (saved by Fritzing 1.0.4)
circuit board: 11.7732cm x 8.2145cm
breadboards: 1

parts:
  U1 = 74HC595 [package="DIP16 [THT]"]
  Part1 = Arduino Uno (Rev3) - ICSP
  R1 = Resistor [tolerance=±5% power=0.25W resistance=220 package=THT]
  LongBeam1 = LED - 5mm [color="White (4500K)" current=0.030A package="5 mm [THT]"]
  LongBeam2 = LED - 5mm [color="White (4500K)" current=0.030A package="5 mm [THT]"]
  LED3 = LED - 3mm [color="White (4500K)" current=0.030A package="3 mm [THT]"]
  LED4 = LED - 3mm [color="White (4500K)" current=0.030A package="3 mm [THT]"]
  R3 = Resistor [tolerance=±5% power=0.25W resistance=220 package=THT]
  LED5 = LED - 3mm [color="White (4500K)" current=0.030A package="3 mm [THT]"]
  LED6 = LED - 3mm [color="White (4500K)" current=0.030A package="3 mm [THT]"]
  LED7 = LED - 3mm [color="White (4500K)" current=0.030A package="3 mm [THT]"]
  LED8 = LED - 3mm [color="White (4500K)" current=0.030A package="3 mm [THT]"]
  R4 = Resistor [tolerance=±5% power=0.25W resistance=220 package=THT]
  LED9 = LED - 3mm [color="Yellow (595nm)" current=0.030A package="3 mm [THT]"]
  LED10 = LED - 3mm [color="Yellow (595nm)" current=0.030A package="3 mm [THT]"]
  LED11 = LED - 3mm [color="Yellow (595nm)" current=0.030A package="3 mm [THT]"]
  LED12 = LED - 3mm [color="Yellow (595nm)" current=0.030A package="3 mm [THT]"]
  LED13 = LED - 3mm [color="Yellow (595nm)" current=0.030A package="3 mm [THT]"]
  LED14 = LED - 3mm [color="Yellow (595nm)" current=0.030A package="3 mm [THT]"]
  LED15 = LED - 5mm [color="Red (660nm)" current=0.030A package="5 mm [THT]"]
  LED16 = LED - 5mm [color="Red (660nm)" current=0.030A package="5 mm [THT]"]
  R5 = Resistor [tolerance=±5% power=0.25W resistance=220 package=THT]
  R6 = Resistor [tolerance=±5% power=0.25W resistance=220 package=THT]
  R7 = Resistor [tolerance=±5% power=0.25W resistance=220 package=THT]
  LED17 = LED - 3mm [color="White (4500K)" current=0.030A package="3 mm [THT]"]
  LED18 = LED - 3mm [color="White (4500K)" current=0.030A package="3 mm [THT]"]
  LED19 = LED - 3mm [color="White (4500K)" current=0.030A package="3 mm [THT]"]
  LED20 = LED - 3mm [color="White (4500K)" current=0.030A package="3 mm [THT]"]
  R8 = Resistor [tolerance=±5% power=0.25W resistance=220 package=THT]
  R9 = Resistor [tolerance=±5% power=0.25W resistance=220 package=THT]
  J2 = female pin header, 2 pins [form="♀ (female)"]  # not connected

nets:
  N1: U1.Q1, R1.Pin_1
  N2: U1.Q2, R3.Pin_1
  N3: U1.Q3, R4.Pin_1
  N4: U1.Q4, R5.Pin_1
  N5: U1.Q5, R6.Pin_1
  N6: U1.Q6, R7.Pin_1
  N7: U1.Q7, R8.Pin_1
  N8: U1.GND, R9.Pin_1
  VCC: U1.MR, U1.VCC, Part1.5V
  N9: U1.SH_CP, Part1.D9_PWM
  N10: U1.ST_CP, Part1.D11_PWM/MOSI
  N11: U1.OE, Part1.GND, LongBeam1.anode, LongBeam2.anode, LED3.anode, LED4.anode, LED5.anode, LED6.anode, LED7.anode, LED8.anode, LED9.anode, LED10.anode, LED11.anode, LED12.anode, LED13.anode, LED14.anode, LED15.anode, LED16.anode, LED17.anode, LED18.anode, LED19.anode, LED20.anode
  N12: U1.DS, Part1.ICSP_MISO, Part1.D12/MISO
  N13: R1.Pin_0, LongBeam1.cathode, LongBeam2.cathode
  N14: LED3.cathode, LED4.cathode, R3.Pin_0
  N15: LED5.cathode, LED6.cathode, LED7.cathode, LED8.cathode, R4.Pin_0
  N16: LED9.cathode, LED10.cathode, LED11.cathode, R5.Pin_0
  N17: LED12.cathode, LED13.cathode, LED14.cathode, R6.Pin_0
  N18: LED15.cathode, LED16.cathode, R7.Pin_0
  N19: LED17.cathode, LED18.cathode, R8.Pin_0
  N20: LED19.cathode, LED20.cathode, R9.Pin_0
